# Fritzing sketch Audioplayback (saved by Fritzing 1.0.4)
breadboards: 1

parts:
  Part1 = Breakout Board for Electret Microphone
  S1 = Momentary Switch [package=tactile-pth]  # not connected
  S2 = Momentary Switch [package=tactile-pth]  # not connected
  LED1 = smd LED [color="Red (633nm)" package="0805 [SMD]"]  # not connected
  LED2 = smd LED [color="Yellow (585nm)" package="1206 [SMD]"]  # not connected
  SP1 = SPEAKER [package=pcb_mount_speaker]
  AMP1 = PAM8403 6W Stereo Amplifier
  U1 = ESP32S-HiLetgo [part_number=ESP32S-HiLetgo]

nets:
  N1: Part1.VCC, U1.3.3
  GND: Part1.GND, AMP1.Ground, U1.GND
  N2: Part1.AUD, U1.GPIO36
  N3: SP1.+, AMP1.R_Out_+
  N4: SP1.-, AMP1.R_Out_-
  N5: AMP1.L_Input, U1.GPIO26
  5V: AMP1.5V, U1.VIN

custom parts:
  PAM8403 6W Stereo Amplifier: PAM8403 6 Watt Stereo Amplifier
  ESP32S-HiLetgo: HiLetgo ESP-WROOM-32 ESP32 ESP-32S Development Board 2.4GHz Dual-Mode WiFi + Bluetooth Dual Cores Microcontroller The ESP32 integrated with Antenna switches, RF Balun, power amplifiers, low-noise amplifiers, filters, and management modules, and the entire solution occupies the least area of PCB. 2.4 GHz Wi-Fi plus Bluetooth dual-mode chip, with TSMC Ultra-low power consumption 40nm technology,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
